# Fritzing sketch MagLock Diagram (saved by Fritzing 0.9.3b)
circuit board: 2.83972cm x 3.41403cm
breadboards: 1

parts:
  R1 = Resistor [tolerance=±5% resistance=1k package=THT]
  L1 = Solenoid
  D1 = Schottky Diode [part_number=1N5817 package="300 mil [THT]"]
  Q1 = npn-Powertransistor [package="TO220 [THT]"]
  JP1 = Header 1 [package=1x01_offset]
  JP2 = Header 1 [package=1x01_offset]
  JP3 = Header 1 [package=1x01_offset]

nets:
  N1: R1.Pin_0, JP1.1
  N2: R1.Pin_1, Q1.base
  10V: L1.pin1, D1.cathode, JP2.1
  N3: L1.pin2, D1.anode, Q1.collector
  GND: Q1.emitter, JP3.1

notes:
  Magnetic Lock Solenoid Raspberry Pi3
  Pi In
  9V
  GND
